// Logisim project gerador-sequencias.circ as structural Verilog: 3 circuits, main circuit main
module main (
);

  wire and_1_out, and_2_out, and_3_out, and_4_out, atrasoPrimeiraSeq_q, atrasoSegundaSeq_q, clock_1_out,
       comparator_1_eq, comparator_2_eq, not_1_out, Select_q;
  wire [3:0] circprimeiraseq_1_saida, circsegundaseq_1_saida, multiplexer_1_out;

  circPrimeiraSeq circprimeiraseq_1 (.Clock(and_1_out), .saida(circprimeiraseq_1_saida));  // open: QA, QB, QC, QD
  Hex_Digit_Display hex_digit_display_1 (.value(circprimeiraseq_1_saida));  // open: dp
  Clock clock_1 (.out(clock_1_out));
  Comparator #(.width(4)) comparator_1 (
    .a(circprimeiraseq_1_saida), .b(4'b0011), .eq(comparator_1_eq));  // open: gt, lt
  and and_1 (and_1_out, clock_1_out, ~and_3_out, not_1_out);  // AND_Gate
  J_K_Flip_Flop Select (.J(and_3_out), .clk(clock_1_out), .K(and_4_out), .Q(Select_q));  // open: Qn, preset, en, reset
  Hex_Digit_Display hex_digit_display_2 (.value(multiplexer_1_out));  // open: dp
  Multiplexer #(.width(4)) multiplexer_1 (
    .in0(circprimeiraseq_1_saida), .in1(circsegundaseq_1_saida), .out(multiplexer_1_out), .sel(Select_q));  // open: en
  and and_2 (and_2_out, clock_1_out, ~and_4_out, Select_q);  // AND_Gate
  not not_1 (not_1_out, Select_q);
  D_Flip_Flop atrasoSegundaSeq (
    .clk(clock_1_out), .D(Select_q), .Q(atrasoSegundaSeq_q));  // open: Qn, preset, en, reset
  circSegundaSeq circsegundaseq_1 (.Clock(and_2_out), .saida(circsegundaseq_1_saida));  // open: QA, QB, QC, QD
  D_Flip_Flop atrasoPrimeiraSeq (
    .clk(clock_1_out), .D(not_1_out), .Q(atrasoPrimeiraSeq_q));  // open: Qn, preset, en, reset
  Hex_Digit_Display hex_digit_display_3 (.value(circsegundaseq_1_saida));  // open: dp
  Comparator #(.width(4)) comparator_2 (.a(circsegundaseq_1_saida), .b(4'b1100), .eq(comparator_2_eq));  // open: gt, lt
  and and_3 (and_3_out, comparator_1_eq, atrasoPrimeiraSeq_q);
  and and_4 (and_4_out, comparator_2_eq, atrasoSegundaSeq_q);

  // Notes on the sheet:
  //   5 12 9 4 6 7 14 8 10 15 3
  //   gerador
  //   7 1 13 10 6 5 15 9 3 4 12
endmodule

module circPrimeiraSeq (
  input  Clock,
  output [3:0] saida,
  output QA,
  output QB,
  output QC,
  output QD
);

  wire and_1_out, and_2_out, and_3_out, and_4_out, and_5_out, and_6_out, and_7_out, not_1_out, not_2_out,
       not_3_out, not_4_out, not_5_out, not_6_out, not_7_out, not_8_out, not_9_out, not_10_out, not_11_out,
       or_1_out, or_2_out, or_3_out, or_4_out, or_5_out, or_6_out;

  J_K_Flip_Flop A (.J(or_6_out), .clk(Clock), .K(or_1_out), .Q(QA));  // open: Qn, preset, en, reset
  J_K_Flip_Flop B (.J(and_5_out), .clk(Clock), .K(or_2_out), .Q(QB));  // open: Qn, preset, en, reset
  J_K_Flip_Flop C (.J(or_3_out), .clk(Clock), .K(QD), .Q(QC));  // open: Qn, preset, en, reset
  J_K_Flip_Flop D (.J(and_4_out), .clk(Clock), .K(QA), .Q(QD));  // open: Qn, preset, en, reset
  not not_1 (not_1_out, QC);
  not not_2 (not_2_out, QD);
  not not_3 (not_3_out, QB);
  not not_4 (not_4_out, QD);
  and and_1 (and_1_out, not_1_out, not_2_out);
  not not_5 (not_5_out, QA);
  and and_2 (and_2_out, QC, not_4_out);
  and and_3 (and_3_out, not_5_out, QC, QD);
  or or_1 (or_1_out, not_3_out, and_2_out);
  or or_2 (or_2_out, and_1_out, and_3_out);
  and and_4 (and_4_out, QA, QC);
  or or_3 (or_3_out, QA, QB);
  not not_6 (not_6_out, QA);
  not not_7 (not_7_out, QC);
  not not_8 (not_8_out, QD);
  or or_4 (or_4_out, not_7_out, not_8_out);
  and and_5 (and_5_out, not_6_out, or_4_out);
  not not_9 (not_9_out, QB);
  not not_10 (not_10_out, QC);
  not not_11 (not_11_out, QD);
  or or_5 (or_5_out, not_10_out, not_11_out);
  and and_6 (and_6_out, not_9_out, QC, QD);
  and and_7 (and_7_out, QB, or_5_out);
  or or_6 (or_6_out, and_6_out, and_7_out);

  assign saida = {QD, QC, QB, QA};
endmodule

module circSegundaSeq (
  input  Clock,
  output [3:0] saida,
  output QA,
  output QB,
  output QC,
  output QD
);

  wire and_1_out, and_2_out, and_3_out, and_4_out, and_5_out, and_6_out, and_7_out, not_1_out, not_2_out,
       not_3_out, not_4_out, not_5_out, not_6_out, not_7_out, not_8_out, not_9_out, not_10_out, or_1_out,
       or_2_out, or_3_out, or_4_out, or_5_out, or_6_out, or_7_out;

  J_K_Flip_Flop A (.J(or_7_out), .clk(Clock), .K(or_3_out), .Q(QA));  // open: Qn, preset, en, reset
  J_K_Flip_Flop B (.J(or_6_out), .clk(Clock), .K(or_1_out), .Q(QB));  // open: Qn, preset, en, reset
  J_K_Flip_Flop C (.J(or_5_out), .clk(Clock), .K(or_4_out), .Q(QC));  // open: Qn, preset, en, reset
  J_K_Flip_Flop D (.J(not_6_out), .clk(Clock), .K(or_2_out), .Q(QD));  // open: Qn, preset, en, reset
  not not_1 (not_1_out, QA);
  not not_2 (not_2_out, QC);
  not not_3 (not_3_out, QC);
  not not_4 (not_4_out, QB);
  not not_5 (not_5_out, QD);
  and and_1 (and_1_out, QB, not_3_out);
  and and_2 (and_2_out, not_4_out, QC, QD);
  or or_1 (or_1_out, QA, not_5_out);
  and and_3 (and_3_out, QA, QB);
  and and_4 (and_4_out, QA, QD);
  or or_2 (or_2_out, not_1_out, not_2_out);
  not not_6 (not_6_out, QB);
  or or_3 (or_3_out, and_1_out, and_2_out);
  or or_4 (or_4_out, and_3_out, and_4_out);
  not not_7 (not_7_out, QA);
  not not_8 (not_8_out, QD);
  or or_5 (or_5_out, not_7_out, not_8_out);
  not not_9 (not_9_out, QB);
  not not_10 (not_10_out, QD);
  and and_5 (and_5_out, QA, QC);
  or or_6 (or_6_out, QD, and_5_out);
  and and_6 (and_6_out, QB, not_10_out);
  and and_7 (and_7_out, not_9_out, QD);
  or or_7 (or_7_out, and_6_out, and_7_out);

  assign saida = {QD, QC, QB, QA};
endmodule
